// Logisim project alu.circ as structural Verilog: 1 circuit, main circuit main
module main (
  input  [31:0] X,
  input  [31:0] Y,
  input  [3:0] Switch,
  output Equal,
  output [31:0] Result
);

  wire comparator_1_lt;
  wire [4:0] bit_extender_1_out, bit_extender_2_out;
  wire [31:0] out_add, out_and, out_div, out_lui, out_mul, out_mulh, out_or, out_rem, out_sll, out_slt,
       out_srl, out_sub, out_xor;

  Bit_Extender #(.in_width(32), .out_width(5)) bit_extender_1 (.in(Y), .out(bit_extender_1_out));
  Bit_Extender #(.in_width(32), .out_width(5)) bit_extender_2 (.in(Y), .out(bit_extender_2_out));
  Shifter #(.width(32)) shifter_1 (.in(X), .\dist (bit_extender_1_out), .out(out_sll));
  Shifter #(.width(32), .shift("lr")) shifter_2 (.in(X), .\dist (bit_extender_2_out), .out(out_srl));
  Adder #(.width(32)) adder_1 (.a(X), .b(Y), .out(out_add));  // open: cin, cout
  assign out_and = X & Y;  // AND_Gate and_1, 32 bits wide
  assign out_or = X | Y;  // OR_Gate or_1, 32 bits wide
  assign out_xor = X ^ Y;  // XOR_Gate xor_1, 32 bits wide
  Comparator #(.width(32)) comparator_1 (.a(X), .b(Y), .eq(Equal), .lt(comparator_1_lt));  // open: gt
  Multiplier #(.width(32)) multiplier_1 (.a(X), .b(Y), .out(out_mul), .cout(out_mulh));  // open: cin
  Divider #(.width(32)) divider_1 (.a(X), .b(Y), .out(out_div), .rem(out_rem));  // open: upper
  assign out_slt = {{31{1'b0}}, comparator_1_lt};  // Bit_Extender bit_extender_3
  Multiplexer #(.select(4), .width(32)) multiplexer_1 (
    .in0(out_sll), .in1(out_srl), .in2(out_add), .in3(out_and), .in4(out_or), .in5(out_xor), .in6(out_slt),
    .in7(out_mul), .in8(out_mulh), .in9(out_div), .in10(out_rem), .in11(out_sub), .in12(out_lui),
    .out(Result), .sel(Switch));  // open: in13, in14, in15, en
  Subtractor #(.width(32)) subtractor_1 (.a(X), .b(Y), .out(out_sub));  // open: bin, bout
  Shifter #(.width(32)) shifter_3 (.in(Y), .\dist (5'b01100), .out(out_lui));

  // Other names for the same wires on the sheet: S[3:0] = Switch

  // Notes on the sheet:
  //   INPUTS to your circuit
  //   DON'T CHANGE THE LOCATIONS OF THE INPUTS AND OUTPUTS!
  //   OUTPUTS from your circuit
endmodule
