// Logisim project cpu.circ as structural Verilog: 21 circuits, main circuit main
module main (
  input  [31:0] INSTRUCTION,
  input  CLOCK,
  output [31:0] FETCH_ADDRESS,
  output [31:0] s0_Value,
  output [31:0] s1_Value,
  output [31:0] t0_Value,
  output [31:0] t1_Value,
  output [31:0] a0_Value,
  output [31:0] ra_Value,
  output [31:0] sp_Value
);

  wire ASel, BrEq, BrLT, BrUn, BSel, MEM_p1, MEM_p3, MEM_p8, MEM_p12, MemRW, nopSel, PCSel, RegWEn;
  wire [1:0] WBSel;
  wire [2:0] ImmSel;
  wire [3:0] ALUSel;
  wire [31:0] ALU, divider_2_out, imm, instr_exec, mem, mem_offset, multiplexer_1_out, multiplexer_2_out,
       multiplexer_3_out, multiplexer_4_out, pc, pc_4, R1, R2, wb;

  Multiplexer #(.width(32), .enable("false")) multiplexer_1 (
    .in0(pc_4), .in1(ALU), .out(multiplexer_1_out), .sel(PCSel));
  Register #(.width(32)) u_PC (.D(multiplexer_1_out), .Q(pc), .clk(CLOCK));  // open: en, clr
  Divider #(.width(32)) divider_1 (.a(pc), .b(32'h4), .out(FETCH_ADDRESS));  // open: upper, rem
  Adder #(.width(32)) adder_1 (.a(pc), .b(32'h4), .out(pc_4));  // open: cin, cout
  Multiplexer #(.width(32), .enable("false")) multiplexer_2 (
    .in0(INSTRUCTION), .in1({32{1'b0}}), .out(multiplexer_2_out), .sel(nopSel));
  Register #(.width(32)) u_INSTR_EXEC (.D(multiplexer_2_out), .Q(instr_exec), .clk(CLOCK));  // open: en, clr
  immgen ImmGen (.instruction(instr_exec), .ImmSel(ImmSel), .imm(imm));
  // Probe on imm
  // Probe on instr_exec[19:15]
  control Control_Unit (
    .instruction(instr_exec), .blt(BrLT), .beq(BrEq), .PCSel(PCSel), .RegWEn(RegWEn), .BrUn(BrUn),
    .ImmSel(ImmSel), .BSel(BSel), .MemRW(MemRW), .WBSel(WBSel), .ASel(ASel), .ALUSel(ALUSel), .nopSel(nopSel));
  regfile_main main_1 (
    .Read_Register_1__rs1(instr_exec[19:15]), .Read_Register_2__rs2(instr_exec[24:20]),
    .Write_Register__rd(instr_exec[11:7]), .Write_Data(wb), .Write_Enable(RegWEn), .Clock(CLOCK),
    .Read_Data_1(R1), .Read_Data_2(R2), .s1_Value(s1_Value), .t0_Value(t0_Value), .t1_Value(t1_Value),
    .a0_Value(a0_Value), .s0_Value(s0_Value), .ra_Value(ra_Value), .sp_Value(sp_Value));
  branchcomp BranchComp (.R1(R1), .R2(R2), .BrUn(BrUn), .BrLt(BrLT), .BrEq(BrEq));
  Multiplexer #(.width(32), .enable("false")) multiplexer_3 (.in0(R1), .in1(pc), .out(multiplexer_3_out), .sel(ASel));
  alu_main main_2 (.Switch(ALUSel), .X(multiplexer_3_out), .Result(ALU), .Y(multiplexer_4_out));  // open: Equal
  Multiplexer #(.width(32), .enable("false")) multiplexer_4 (.in0(R2), .in1(imm), .out(multiplexer_4_out), .sel(BSel));
  // Probe on ALU
  // Probe on ALUSel
  Divider #(.width(32)) divider_2 (.a(ALU), .b(32'h4), .out(divider_2_out));  // open: upper, rem
  // mem_main MEM: pin names not known; wires that end beside it: MEM_p1, MEM_p1, MEM_p3, MEM_p3, divider_2_out, R2, MemRW, MEM_p8, CLOCK, MEM_p8, mem, MEM_p12
  loadOffset load (.mem(mem), .offset(ALU), .funct3(instr_exec[14:12]), .data(mem_offset));
  // Probe on wb
  Multiplexer #(.select(2), .width(32), .enable("false")) multiplexer_5 (
    .in0(mem_offset), .in1(ALU), .in2(pc), .out(wb), .sel(WBSel));  // open: in3
  // Probe on WBSel

  // Other names for the same wires on the sheet: a0[31:0] = a0_Value; clk = CLOCK; fetch_addr[31:0] = FETCH_ADDRESS;
  //   ra[31:0] = ra_Value; s0[31:0] = s0_Value; s1[31:0] = s1_Value; sp[31:0] = sp_Value; t0[31:0] = t0_Value;
  //   t1[31:0] = t1_Value

  // Notes on the sheet:
  //   Output
  //   These are outputs/inputs from run.circ
  //   Inputs
  //   These are DEBUG/TEST outputs from your circuit.
endmodule

module opcode_identifier (
  input  [31:0] Instruction,
  output [31:0] LOADS,
  output [31:0] I_TYPE,
  output [31:0] S_TYPE,
  output [31:0] R_TYPE,
  output [31:0] U_TYPE,
  output [31:0] SB_TYPE,
  output [31:0] JALR,
  output [31:0] UJ_TYPE
);

  // Probe on Instruction[6:2]
  Demultiplexer #(.select(5), .width(32), .enable("false")) demultiplexer_1 (
    .out0(LOADS), .out4(I_TYPE), .out8(S_TYPE), .out12(R_TYPE), .out13(U_TYPE), .out24(SB_TYPE),
    .out25(JALR), .out27(UJ_TYPE), .in(Instruction), .sel(Instruction[6:2]));  // open: out1, out2, out3, out5, out6, out7, out9, out10, out11, out14, out15, out16, out17, out18, out19, out20, out21, out22, out23, out26, out28, out29, out30, out31
endmodule

module RSplit (
  input  [31:0] Instruction,
  output [6:0] opcode,
  output [4:0] rd,
  output [2:0] funct3,
  output [4:0] rs1,
  output [4:0] rs2,
  output [6:0] funct7
);


  assign funct3 = Instruction[14:12];
  assign funct7 = Instruction[31:25];
  assign opcode = Instruction[6:0];
  assign rd = Instruction[11:7];
  assign rs1 = Instruction[19:15];
  assign rs2 = Instruction[24:20];
endmodule

module ISplit (
  input  [31:0] Instruction
);


  // Other names for the same wires on the sheet: RD[4:0] = Instruction[11:7]; FUNCT3[2:0] = Instruction[14:12];
  //   RS1[4:0] = Instruction[19:15]; RS2[4:0] = Instruction[24:20]; FUNCT7[6:0] = Instruction[31:25]
endmodule

module control (
  input  [31:0] instruction,
  input  blt,
  input  beq,
  output PCSel,
  output [2:0] ImmSel,
  output RegWEn,
  output BrUn,
  output BSel,
  output ASel,
  output [3:0] ALUSel,
  output MemRW,
  output [1:0] WBSel,
  output nopSel
);

  PCSel pcsel_1 (.beq(beq), .blt(blt), .opcode(instruction[6:0]), .funct3(instruction[14:12]), .PCSel(PCSel));
  ImmSel immsel_1 (.opcode(instruction[6:0]), .ImmSel(ImmSel));
  RegWEn regwen_1 (.opcode(instruction[6:0]), .RegWEn(RegWEn));
  BrUn brun_1 (.instruction(instruction), .BrUn(BrUn));
  BSel bsel_1 (.opcode(instruction[6:0]), .BSel(BSel));
  ASel asel_1 (.opcode(instruction[6:0]), .ASel(ASel));
  ALUSel alusel_1 (.Instruction(instruction), .ALUSel(ALUSel));
  MemRW memrw_1 (.opcode(instruction[6:0]), .MemRW(MemRW));
  WBSel wbsel_1 (.opcode(instruction[6:0]), .WBSel(WBSel));
  nopSel nopsel_1 (.funct3(instruction[14:12]), .opcode(instruction[6:0]), .beq(beq), .blt(blt), .nopSel(nopSel));

  // Other names for the same wires on the sheet: opcode[6:0] = instruction[6:0]; funct3[2:0] = instruction[14:12]
endmodule

module PCSel (
  input  beq,
  input  blt,
  input  [6:0] opcode,
  input  [2:0] funct3,
  output PCSel
);

  wire branch, multiplexer_1_out, multiplexer_2_out;

  Multiplexer #(.enable("false")) multiplexer_1 (.in0(1'b0), .in1(1'b1), .out(multiplexer_1_out), .sel(beq));
  Multiplexer #(.enable("false")) multiplexer_2 (.in0(1'b0), .in1(1'b1), .out(multiplexer_2_out), .sel(blt));
  Multiplexer #(.select(3), .enable("false")) multiplexer_3 (
    .in0(multiplexer_1_out), .in4(multiplexer_2_out), .in6(multiplexer_2_out), .out(branch), .sel(funct3));  // open: in1, in2, in3, in5, in7
  Multiplexer #(.select(5), .enable("false")) multiplexer_4 (
    .in0(1'b0), .in4(1'b0), .in8(1'b0), .in12(1'b0), .in13(1'b0), .in24(branch), .in25(1'b1), .in27(1'b1),
    .out(PCSel), .sel(opcode[6:2]));  // open: in1, in2, in3, in5, in6, in7, in9, in10, in11, in14, in15, in16, in17, in18, in19, in20, in21, in22, in23, in26, in28, in29, in30, in31
endmodule

module RegWEn (
  input  [6:0] opcode,
  output RegWEn
);

  wire comparator_1_eq, comparator_2_eq, or_1_out;

  Comparator #(.width(7)) comparator_1 (.a(opcode), .b(7'b0100011), .eq(comparator_1_eq));  // open: gt, lt
  Comparator #(.width(7)) comparator_2 (.a(opcode), .b(7'b1100011), .eq(comparator_2_eq));  // open: gt, lt
  not not_1 (RegWEn, or_1_out);
  or or_1 (or_1_out, comparator_1_eq, comparator_2_eq);
endmodule

module BrUn (
  input  [31:0] instruction,
  output BrUn
);

  wire comparator_1_eq, comparator_2_eq;

  Comparator #(.width(7)) comparator_1 (.a(instruction[6:0]), .b(7'b1100011), .eq(comparator_1_eq));  // open: gt, lt
  Comparator #(.width(3)) comparator_2 (.a(instruction[14:12]), .b(3'b110), .eq(comparator_2_eq));  // open: gt, lt
  and and_1 (BrUn, comparator_1_eq, comparator_2_eq);
endmodule

module ImmSel (
  input  [6:0] opcode,
  output [2:0] ImmSel
);

  Multiplexer #(.select(5), .width(3), .enable("false")) multiplexer_1 (
    .in0(3'b001), .in4(3'b001), .in8(3'b010), .in12(3'b000), .in13(3'b100), .in24(3'b011), .in25(3'b110),
    .in27(3'b101), .out(ImmSel), .sel(opcode[6:2]));  // open: in1, in2, in3, in5, in6, in7, in9, in10, in11, in14, in15, in16, in17, in18, in19, in20, in21, in22, in23, in26, in28, in29, in30, in31
endmodule

module BSel (
  input  [6:0] opcode,
  output BSel
);

  wire comparator_1_eq;

  Comparator #(.width(7)) comparator_1 (.a(opcode), .b(7'b0110011), .eq(comparator_1_eq));  // open: gt, lt
  not not_1 (BSel, comparator_1_eq);
endmodule

module MemRW (
  input  [6:0] opcode,
  output MemRW
);

  Comparator #(.width(7)) comparator_1 (.a(opcode), .b(7'b0100011), .eq(MemRW));  // open: gt, lt
endmodule

module WBSel (
  input  [6:0] opcode,
  output [1:0] WBSel
);

  Multiplexer #(.select(5), .width(2), .enable("false")) multiplexer_1 (
    .in0(2'b00), .in1(2'b01), .in4(2'b01), .in8(2'b01), .in12(2'b01), .in13(2'b01), .in24(2'b01),
    .in25(2'b10), .in27(2'b10), .out(WBSel), .sel(opcode[6:2]));  // open: in2, in3, in5, in6, in7, in9, in10, in11, in14, in15, in16, in17, in18, in19, in20, in21, in22, in23, in26, in28, in29, in30, in31
endmodule

module ASel (
  input  [6:0] opcode,
  output ASel
);

  Multiplexer #(.select(5), .enable("false")) multiplexer_1 (
    .in0(1'b0), .in4(1'b0), .in8(1'b0), .in12(1'b0), .in13(1'b0), .in24(1'b1), .in25(1'b0), .in27(1'b1),
    .out(ASel), .sel(opcode[6:2]));  // open: in1, in2, in3, in5, in6, in7, in9, in10, in11, in14, in15, in16, in17, in18, in19, in20, in21, in22, in23, in26, in28, in29, in30, in31
endmodule

module R_ALU (
  input  [2:0] funct3,
  input  [6:0] funct7,
  output [3:0] R_type
);

  wire [3:0] multiplexer_1_out, multiplexer_2_out, multiplexer_3_out, subfix_1_output;

  subfix subfix_1 (.funct7(funct7), .add(4'b0010), .mul(4'b0111), .sub(4'b1011), .\output (subfix_1_output));
  Multiplexer #(.width(4), .enable("false")) multiplexer_1 (
    .in0(4'b0000), .in1(4'b1000), .out(multiplexer_1_out), .sel(funct7[0]));
  Multiplexer #(.width(4), .enable("false")) multiplexer_2 (
    .in0(4'b0101), .in1(4'b1001), .out(multiplexer_2_out), .sel(funct7[0]));
  Multiplexer #(.width(4), .enable("false")) multiplexer_3 (
    .in0(4'b0100), .in1(4'b1010), .out(multiplexer_3_out), .sel(funct7[0]));
  Multiplexer #(.select(3), .width(4), .enable("false")) multiplexer_4 (
    .in0(subfix_1_output), .in1(multiplexer_1_out), .in2(4'b0110), .in4(multiplexer_2_out), .in5(4'b0001),
    .in6(multiplexer_3_out), .in7(4'b0011), .out(R_type), .sel(funct3));  // open: in3

  // Other names for the same wires on the sheet: funct7lsb = funct7[0]

  // Notes on the sheet:
  //   add
  //   mul
  //   sub
  //   sll
  //   mulh
  //   xor
  //   div
  //   or
  //   rem
  //   slt
  //   srl
  //   and
endmodule

module I_ALU (
  input  [2:0] funct3,
  output [3:0] I_type
);

  Multiplexer #(.select(3), .width(4), .enable("false")) multiplexer_1 (
    .in0(4'b0010), .in1(4'b0000), .in2(4'b0110), .in4(4'b0101), .in5(4'b0001), .in6(4'b0100), .in7(4'b0011),
    .out(I_type), .sel(funct3));  // open: in3

  // Notes on the sheet:
  //   add
  //   sll
  //   slt
  //   xor
  //   srl
  //   or
  //   and
endmodule

module ALUSel (
  input  [31:0] Instruction,
  output [3:0] ALUSel
);

  wire [3:0] I_type_i_type, R_type_r_type;

  I_ALU I_type (.funct3(Instruction[14:12]), .I_type(I_type_i_type));
  R_ALU R_type (.funct3(Instruction[14:12]), .funct7(Instruction[31:25]), .R_type(R_type_r_type));
  Multiplexer #(.select(5), .width(4), .enable("false")) multiplexer_1 (
    .in0(4'b0010), .in4(I_type_i_type), .in8(4'b0010), .in12(R_type_r_type), .in13(4'b1100), .in24(4'b0010),
    .in25(4'b0010), .in27(4'b0010), .out(ALUSel), .sel(Instruction[6:2]));  // open: in1, in2, in3, in5, in6, in7, in9, in10, in11, in14, in15, in16, in17, in18, in19, in20, in21, in22, in23, in26, in28, in29, in30, in31

  // Other names for the same wires on the sheet: opcode[4:0] = Instruction[6:2]; funct3[2:0] = Instruction[14:12];
  //   funct7[6:0] = Instruction[31:25]

  // Notes on the sheet:
  //   add
  //   lui
endmodule

module subfix (
  input  [6:0] funct7,
  input  [3:0] add,
  input  [3:0] mul,
  input  [3:0] sub,
  output [3:0] \output 
);

  Multiplexer #(.select(2), .width(4), .enable("false")) multiplexer_1 (
    .in0(add), .in1(mul), .in2(sub), .out(\output ), .sel({funct7[5], funct7[0]}));  // open: in3

  // Notes on the sheet:
  //   This subcircuit is to cover the sub instruction in R-types
endmodule

module branchcomp (
  input  [31:0] R1,
  input  [31:0] R2,
  input  BrUn,
  output BrLt,
  output BrEq
);

  wire comparator_1_lt, comparator_2_lt;

  Comparator #(.width(32)) comparator_1 (.a(R1), .b(R2), .lt(comparator_1_lt));  // open: gt, eq
  Comparator #(.width(32), .mode("unsigned")) comparator_2 (.a(R1), .b(R2), .lt(comparator_2_lt));  // open: gt, eq
  Comparator #(.width(32)) comparator_3 (.a(R1), .b(R2), .eq(BrEq));  // open: gt, lt
  Multiplexer #(.enable("false")) multiplexer_1 (.in0(comparator_1_lt), .in1(comparator_2_lt), .out(BrLt), .sel(BrUn));

  // Notes on the sheet:
  //   2's Complement
  //   Unsigned
endmodule

module immgen (
  input  [31:0] instruction,
  input  [2:0] ImmSel,
  output [31:0] imm
);

  wire [31:0] bit_extender_3_out, bit_extender_5_out, I_type, jalr, S_type, SB_type, shifter_1_out,
       shifter_2_out, U_type, UJ_type;

  assign I_type = {{20{instruction[31]}}, instruction[31:20]};  // Bit_Extender bit_extender_1
  assign S_type = {{20{instruction[31]}}, {instruction[31:25], instruction[11:7]}};  // Bit_Extender bit_extender_2
  assign bit_extender_3_out = {{20{instruction[31]}}, {instruction[31], instruction[7], instruction[30:25], instruction[11:8]}};  // Bit_Extender bit_extender_3
  assign U_type = {{12{instruction[31]}}, instruction[31:12]};  // Bit_Extender bit_extender_4
  assign bit_extender_5_out = {{12{instruction[31]}}, {instruction[31], instruction[19:12], instruction[20], instruction[30:21]}};  // Bit_Extender bit_extender_5
  assign jalr = {{20{instruction[31]}}, instruction[31:20]};  // Bit_Extender bit_extender_6
  Shifter #(.width(32)) shifter_1 (.in(bit_extender_3_out), .\dist (5'b00001), .out(shifter_1_out));
  Shifter #(.width(32)) shifter_2 (.in(bit_extender_5_out), .\dist (5'b00001), .out(shifter_2_out));
  Subtractor #(.width(32)) subtractor_1 (.a(shifter_1_out), .b(32'h4), .out(SB_type));  // open: bin, bout
  Subtractor #(.width(32)) subtractor_2 (.a(shifter_2_out), .b(32'h4), .out(UJ_type));  // open: bin, bout
  Multiplexer #(.select(3), .width(32), .enable("false")) multiplexer_1 (
    .in0({32{1'b0}}), .in1(I_type), .in2(S_type), .in3(SB_type), .in4(U_type), .in5(UJ_type), .in6(jalr),
    .out(imm), .sel(ImmSel));  // open: in7

  // Notes on the sheet:
  //   Inputs
  //   Output
endmodule

module nopSel (
  input  [2:0] funct3,
  input  [6:0] opcode,
  input  beq,
  input  blt,
  output nopSel
);

  wire branch, multiplexer_1_out, multiplexer_2_out;

  Multiplexer #(.enable("false")) multiplexer_1 (.in0(1'b0), .in1(1'b1), .out(multiplexer_1_out), .sel(beq));
  Multiplexer #(.enable("false")) multiplexer_2 (.in0(1'b0), .in1(1'b1), .out(multiplexer_2_out), .sel(blt));
  Multiplexer #(.select(3), .enable("false")) multiplexer_3 (
    .in0(multiplexer_1_out), .in4(multiplexer_2_out), .in6(multiplexer_2_out), .out(branch), .sel(funct3));  // open: in1, in2, in3, in5, in7
  Multiplexer #(.select(5), .enable("false")) multiplexer_4 (
    .in0(1'b0), .in4(1'b0), .in8(1'b0), .in12(1'b0), .in13(1'b0), .in24(branch), .in25(1'b1), .in27(1'b1),
    .out(nopSel), .sel(opcode[6:2]));  // open: in1, in2, in3, in5, in6, in7, in9, in10, in11, in14, in15, in16, in17, in18, in19, in20, in21, in22, in23, in26, in28, in29, in30, in31

  // Other names for the same wires on the sheet: op5[4:0] = opcode[6:2]
endmodule

module loadOffset (
  input  [31:0] mem,
  input  [31:0] offset,
  input  [2:0] funct3,
  output [31:0] data
);

  wire [7:0] multiplexer_1_out;
  wire [15:0] multiplexer_2_out;
  wire [31:0] bit_extender_1_out, bit_extender_2_out;

  Multiplexer #(.select(2), .width(8), .enable("false")) multiplexer_1 (
    .in0(mem[7:0]), .in1(mem[15:8]), .in2(mem[23:16]), .in3(mem[31:24]), .out(multiplexer_1_out),
    .sel(offset[1:0]));
  Multiplexer #(.width(16), .enable("false")) multiplexer_2 (
    .in0(mem[15:0]), .in1(mem[31:16]), .out(multiplexer_2_out), .sel(offset[1]));
  assign bit_extender_1_out = {{24{multiplexer_1_out[7]}}, multiplexer_1_out};  // Bit_Extender bit_extender_1
  assign bit_extender_2_out = {{16{multiplexer_2_out[15]}}, multiplexer_2_out};  // Bit_Extender bit_extender_2
  Multiplexer #(.select(2), .width(32), .enable("false")) multiplexer_3 (
    .in0(bit_extender_1_out), .in1(bit_extender_2_out), .in2(mem), .out(data), .sel(funct3[1:0]));  // open: in3

  // Other names for the same wires on the sheet: funct3_t[1:0] = funct3[1:0]
endmodule
