// Logisim project regfile.circ as structural Verilog: 5 circuits, main circuit main
// ra
module main (
  input  [4:0] Read_Register_1__rs1,
  input  [4:0] Read_Register_2__rs2,
  input  [4:0] Write_Register__rd,
  input  [31:0] Write_Data,
  input  Write_Enable,
  input  Clock,
  output [31:0] s0_Value,
  output [31:0] s1_Value,
  output [31:0] t0_Value,
  output [31:0] t1_Value,
  output [31:0] a0_Value,
  output [31:0] ra_Value,
  output [31:0] sp_Value,
  output [31:0] Read_Data_1,
  output [31:0] Read_Data_2
);

  wire a0_en, a1_en, ra_en, s0_en, s1_en, sp_en, t0_en, t1_en;
  wire [31:0] a1, zero;

  regwrite regwrite (
    .write_enable(Write_Enable), .switch(Write_Register__rd), .ra(ra_en), .sp(sp_en), .t0(t0_en), .t1(t1_en),
    .s0(s0_en), .s1(s1_en), .a0(a0_en), .a1(a1_en));
  regdata regdata (
    .x0(zero), .ra(ra_Value), .sp(sp_Value), .t0(t0_Value), .t1(t1_Value), .s0(s0_Value), .s1(s1_Value),
    .a0(a0_Value), .a1(a1), .read_data1(Read_Data_1), .read_data2(Read_Data_2),
    .read_reg1(Read_Register_1__rs1), .read_reg2(Read_Register_2__rs2));
  regs registers (
    .write_data(Write_Data), .clock(Clock), .ra_en(ra_en), .t0_en(t0_en), .sp_en(sp_en), .t1_en(t1_en),
    .s0_en(s0_en), .a0_en(a0_en), .s1_en(s1_en), .a1_en(a1_en), .ra(ra_Value), .t0(t0_Value), .s0(s0_Value),
    .a0(a0_Value), .sp(sp_Value), .t1(t1_Value), .s1(s1_Value), .a1(a1), .zero(zero));

  // Other names for the same wires on the sheet: a0[31:0] = a0_Value; clk = Clock; ra[31:0] = ra_Value;
  //   read_data1[31:0] = Read_Data_1; read_data2[31:0] = Read_Data_2; read_reg1[4:0] = Read_Register_1__rs1;
  //   read_reg2[4:0] = Read_Register_2__rs2; s0[31:0] = s0_Value; s1[31:0] = s1_Value; sp[31:0] = sp_Value;
  //   t0[31:0] = t0_Value; t1[31:0] = t1_Value; write_en = Write_Enable; write_reg[4:0] = Write_Register__rd

  // Notes on the sheet:
  //   INPUTS to your circuit
  //   These are DEBUG/TEST outputs from your circuit.
  //   DON'T CHANGE THE LOCATIONS OF THE INPUTS AND OUTPUTS!
  //   OUTPUTS from your circuit
endmodule

module regdecide (
  input  [31:0] x0,
  input  [31:0] ra,
  input  [31:0] sp,
  input  [31:0] t0,
  input  [31:0] t1,
  input  [31:0] s0,
  input  [31:0] s1,
  input  [31:0] a0,
  input  [31:0] a1,
  input  [4:0] Switch,
  output [31:0] Data
);

  Multiplexer #(.select(5), .width(32), .enable("false")) multiplexer_1 (
    .in0(x0), .in1(ra), .in2(sp), .in5(t0), .in6(t1), .in8(s0), .in9(s1), .in10(a0), .in11(a1), .out(Data),
    .sel(Switch));  // open: in3, in4, in7, in12, in13, in14, in15, in16, in17, in18, in19, in20, in21, in22, in23, in24, in25, in26, in27, in28, in29, in30, in31
endmodule

module regdata (
  input  [31:0] x0,
  input  [31:0] ra,
  input  [31:0] sp,
  input  [31:0] t0,
  input  [31:0] t1,
  input  [31:0] s0,
  input  [31:0] s1,
  input  [31:0] a0,
  input  [31:0] a1,
  input  [4:0] read_reg1,
  input  [4:0] read_reg2,
  output [31:0] read_data1,
  output [31:0] read_data2
);

  regdecide RS1 (
    .t1(t1), .t0(t0), .sp(sp), .ra(ra), .x0(x0), .s0(s0), .s1(s1), .a0(a0), .a1(a1), .Data(read_data1),
    .Switch(read_reg1));
  regdecide RS2 (
    .t1(t1), .t0(t0), .sp(sp), .ra(ra), .x0(x0), .s0(s0), .s1(s1), .a0(a0), .a1(a1), .Data(read_data2),
    .Switch(read_reg2));

  // Other names for the same wires on the sheet: zero[31:0] = x0
endmodule

module regwrite (
  input  [4:0] switch,
  input  write_enable,
  output ra,
  output sp,
  output t0,
  output t1,
  output s0,
  output s1,
  output a0,
  output a1
);

  Demultiplexer #(.select(5), .disabled(0), .enable("false")) demultiplexer_1 (
    .out1(ra), .out2(sp), .out5(t0), .out6(t1), .out8(s0), .out9(s1), .out10(a0), .out11(a1),
    .in(write_enable), .sel(switch));  // open: out0, out3, out4, out7, out12, out13, out14, out15, out16, out17, out18, out19, out20, out21, out22, out23, out24, out25, out26, out27, out28, out29, out30, out31
endmodule

module regs (
  input  [31:0] write_data,
  input  clock,
  input  ra_en,
  input  sp_en,
  input  t0_en,
  input  t1_en,
  input  s0_en,
  input  s1_en,
  input  a0_en,
  input  a1_en,
  output [31:0] zero,
  output [31:0] ra,
  output [31:0] sp,
  output [31:0] t0,
  output [31:0] t1,
  output [31:0] s0,
  output [31:0] s1,
  output [31:0] a0,
  output [31:0] a1
);

  Register #(.width(32)) u_zero (.Q(zero));  // open: D, en, clk, clr
  Register #(.width(32)) u_ra (.D(write_data), .en(ra_en), .Q(ra), .clk(clock));  // open: clr
  Register #(.width(32)) u_t0 (.D(write_data), .en(t0_en), .Q(t0), .clk(clock));  // open: clr
  Register #(.width(32)) u_s0 (.D(write_data), .en(s0_en), .Q(s0), .clk(clock));  // open: clr
  Register #(.width(32)) u_a0 (.D(write_data), .en(a0_en), .Q(a0), .clk(clock));  // open: clr
  Register #(.width(32)) u_sp (.D(write_data), .en(sp_en), .Q(sp), .clk(clock));  // open: clr
  Register #(.width(32)) u_t1 (.D(write_data), .en(t1_en), .Q(t1), .clk(clock));  // open: clr
  Register #(.width(32)) u_s1 (.D(write_data), .en(s1_en), .Q(s1), .clk(clock));  // open: clr
  Register #(.width(32)) u_a1 (.D(write_data), .en(a1_en), .Q(a1), .clk(clock));  // open: clr

  // Other names for the same wires on the sheet: clk = clock
endmodule
